# Fritzing sketch Chas_challenge_G8 (saved by Fritzing 1.0.4)
breadboards: 1

parts:
  Arduino_Uno_R4_Wifi = Arduino UNO R4 WiFi
  Sparkfun_ENS160/BME280_combo = SparkFun Environmental Combo Breakout - ENS160/BME280 (Qwiic) [part_number=SEN-22858]
  A2 = BBAA100043
  SPS30 = IC, SIP package, 5 pins [chip_label=SPS30]
  SDA_SPS30_resistor = Resistor [tolerance=±5% power=0.25W resistance=10k package=THT]
  SCL_SPS30_resistor = Resistor [tolerance=±5% power=0.25W resistance=10k package=THT]
  R1 = Resistor [tolerance=±5% power=0.25W resistance=1k package=THT]
  R2 = Resistor [tolerance=±5% power=0.25W resistance=1k package=THT]
  R3 = Resistor [tolerance=±5% power=0.25W resistance=1k package=THT]

nets (from the schematic view):
  5V wire: Arduino_Uno_R4_Wifi.Pin_8, SPS30.pin1, SDA_SPS30_resistor.Pin_0, SCL_SPS30_resistor.Pin_0
  GND wire: Arduino_Uno_R4_Wifi.Pin_9, Arduino_Uno_R4_Wifi.Pin_18, Sparkfun_ENS160/BME280_combo.GND, A2.pin4, SPS30.pin4, SPS30.pin5
  N1: Arduino_Uno_R4_Wifi.Pin_16, SPS30.pin2, SDA_SPS30_resistor.Pin_1
  N2: Arduino_Uno_R4_Wifi.Pin_17, SPS30.pin3, SCL_SPS30_resistor.Pin_1
  N3: Arduino_Uno_R4_Wifi.Pin_19, Sparkfun_ENS160/BME280_combo.3.3V
  N4: Arduino_Uno_R4_Wifi.Pin_20, Sparkfun_ENS160/BME280_combo.SDA
  N5: Arduino_Uno_R4_Wifi.Pin_21, Sparkfun_ENS160/BME280_combo.SCL
  N6: Arduino_Uno_R4_Wifi.Pin_39, R1.Pin_0
  N7: Arduino_Uno_R4_Wifi.Pin_40, R2.Pin_1
  N8: Arduino_Uno_R4_Wifi.Pin_41, R3.Pin_1
  N9: A2.pin1, R3.Pin_0
  N10: A2.pin2, R2.Pin_0
  N11: A2.pin3, R1.Pin_1

custom parts:
  Arduino UNO R4 WiFi: The Arduino UNO R4 WiFi merges the RA4M1 microprocessor from Renesas with the ESP32-S3 from Espressif, creating an all-in-one tool for makers with enhanced processing power and a diverse array of new peripherals.
  SparkFun Environmental Combo Breakout - ENS160/BME280 (Qwiic): Description The SparkFun ENS160/BME280 Environmental Combo Breakout takes care of all your atmospheric-quality sensing needs with the popular ENS160 and BME280 ICs. This unique breakout provides various environmental data, including AQI, TVOCs, equivalent CO2 (or eCO2) levels, barometric pressure, humidity, and temperature. To make it even easier to use this breakout, all communication is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
  BBAA100043: BBAA100043 traffic light module.
